# Fritzing sketch cdstest (saved by Fritzing 0.9.3b)
breadboards: 1

parts:
  Raspberry_Pi_1 = Raspberry Pi 3 [part_number=RPI-3-V1.2]
  R1 = Trimmer Potentiometer [maximum_resistance=10kΩ package=THT]
  R2 = Resistor [tolerance=±5% resistance=220 package=THT]
  R3 = Photocell (LDR) [package=THT]
  LED1 = LED - 5mm [color="Red (633nm)" package="5 mm [THT]"]

nets:
  3V3: Raspberry_Pi_1.3v3, Raspberry_Pi_1.3V3, Raspberry_Pi_1.GPIO23, R3.pin_0, LED1.anode
  N1: Raspberry_Pi_1.GPIO17, R1.leg1, R1.wiper, R3.pin_1
  N2: Raspberry_Pi_1.GND, R1.leg2, R2.Pin_1
  N3: R2.Pin_0, LED1.cathode
