# Fritzing sketch ledtest (saved by Fritzing 0.9.3b)
breadboards: 1

parts:
  Raspberry_Pi_1 = Raspberry Pi 3 [part_number=RPI-3-V1.2]
  R1 = Resistor [tolerance=±5% resistance=1k package=THT]
  LED1 = LED - 5mm [color="Green (555nm)" package="5 mm [THT]"]
  LED2 = LED - 5mm [color="Yellow (574nm)" package="5 mm [THT]"]
  LED3 = LED - 5mm [color="Red (633nm)" package="5 mm [THT]"]

nets:
  N1: Raspberry_Pi_1.GPIO4, LED1.anode
  N2: Raspberry_Pi_1.GPIO17, LED2.anode
  N3: Raspberry_Pi_1.GPIO27, LED3.anode
  N4: Raspberry_Pi_1.GND, R1.Pin_0
  N5: R1.Pin_1, LED1.cathode, LED2.cathode, LED3.cathode
