# Fritzing sketch pullup_down (saved by Fritzing 0.9.3b)
breadboards: 2

parts:
  Raspberry_Pi_1 = Raspberry Pi 3 [part_number=RPI-3-V1.2]
  S1 = Pushbutton [package="[THT]"]
  R1 = Resistor [tolerance=±5% resistance=220 package=THT]
  Raspberry_Pi_2 = Raspberry Pi 3 [part_number=RPI-3-V1.2]
  S2 = Pushbutton [package="[THT]"]
  R2 = Resistor [tolerance=±5% resistance=220 package=THT]

nets:
  N1: Raspberry_Pi_1.3v3, R1.Pin_0
  N2: Raspberry_Pi_1.GPIO4, S1.Pin_3, S1.Pin_4, R1.Pin_1
  N3: Raspberry_Pi_1.GND, S1.Pin_1, S1.Pin_2
  N4: Raspberry_Pi_2.3v3, S2.Pin_3, S2.Pin_4
  N5: Raspberry_Pi_2.GPIO4, S2.Pin_1, S2.Pin_2, R2.Pin_0
  N6: Raspberry_Pi_2.GND, R2.Pin_1

notes:
  Pull-Up
  Pull-Down
