# Fritzing sketch switchtest (saved by Fritzing 0.9.3b)
breadboards: 1

parts:
  Raspberry_Pi_1 = Raspberry Pi 3 [part_number=RPI-3-V1.2]
  S1 = Pushbutton [package="[THT]"]
  R1 = Resistor [tolerance=±5% resistance=220 package=THT]
  R2 = Resistor [tolerance=±5% resistance=220 package=THT]
  LED1 = LED - 5mm [color="Red (633nm)" package="5 mm [THT]"]

nets:
  N1: Raspberry_Pi_1.3v3, S1.Pin_3, S1.Pin_4
  N2: Raspberry_Pi_1.GPIO4, S1.Pin_1, S1.Pin_2, R1.Pin_0
  N3: Raspberry_Pi_1.GPIO18, R2.Pin_0
  N4: Raspberry_Pi_1.GND, R1.Pin_1, LED1.cathode
  N5: R2.Pin_1, LED1.anode
